# Fritzing sketch buck schem (saved by Fritzing 0.9.10b)

parts:
  Q2 = NPN-Transistor [package="TO92 [THT]"]
  R3 = Resistor [tolerance=±5% power=0.25 resistance=10k package=THT]
  C5 = Ceramic Capacitor [capacitance=470pF voltage=35V part_number="(to speed-up switching)" package="100 mil [THT, multilayer]"]
  Q1 = NPN-Transistor [package="TO92 [THT]"]
  R2 = Resistor [tolerance=±5% power=0.25 resistance=22k package=THT]
  L1 = Inductor [inductance=470µH current=3A package="400 mil [THT]"]
  Q4 = Basic FET P-Channel [package="TO220 [THT]"]
  Part1 = Arduino Nano (Rev3.0)
  R5 = Resistor [tolerance=±5% power=0.25 resistance=1k package=THT]
  D2 = Schottky Diode [part_number="1N5817 (prevent saturation to speed-up switching)" package="300 mil [THT]"]
  R7 = Resistor [tolerance=±5% power=0.25 resistance=100 package=THT]
  C3 = Ceramic Capacitor [capacitance=1µF voltage=35V part_number="(bypass cap)" package="100 mil [THT, multilayer]"]
  C2 = Electrolytic Capacitor [capacitance=100µF voltage=35V package="100 mil [THT, electrolytic]"]
  Q3 = PNP-Transistor [package="TO92 [THT]"]
  C1 = Electrolytic Capacitor [capacitance=100µF voltage=35V package="100 mil [THT, electrolytic]"]
  R4 = Resistor [tolerance=±5% power=0.25 resistance=33 part_number="(to limit switching current)" package=THT]
  C4 = Ceramic Capacitor [capacitance=1µF voltage=35V part_number="(bypass cap)" package="100 mil [THT, multilayer]"]
  R1 = TRIMPOT [maximum_resistance=50kΩ knob_status=50% power=0.5W package=3386u]
  D1 = Schottky Diode [part_number=1N5822 package="300 mil [THT]"]
  R6 = Resistor [tolerance=±5% power=0.25 resistance=820 package=THT]

nets:
  N1: Q2.E, Q3.E, R4.Pin_0
  N2: Q2.B, Q1.C, R5.Pin_0, D2.cathode, Q3.B
  7-12V: Q2.C, Q4.source, Part1.VIN, R5.Pin_1, C3.1, C2.+, C4.1
  GND: R3.Pin_0, Q1.E, Part1.GND, C3.0, C2.-, Q3.C, C1.-, C4.0, R1.CCW, D1.anode
  N3: R3.Pin_1, R2.Pin_0, Part1.A1
  N4: C5.0, Q1.B, D2.anode, R6.Pin_1
  N5: C5.1, R7.Pin_1, R6.Pin_0
  Vout: R2.Pin_1, L1.pin_1, C1.+
  N6: L1.pin_0, Q4.drain, D1.cathode
  N7: Q4.gate, R4.Pin_1
  N8: Part1.D3, R7.Pin_0
  N9: Part1.5V, R1.CW
  N10: Part1.A0, R1.WIPER

notes:
  Level shift
  (5V to 7-12V)
  Push-pull driver
  (for steep switching)
  Buck converter
  Baker clamp
