# Fritzing sketch Voltage clamp for PV (saved by Fritzing 0.9.10b)
breadboards: 1

parts:
  Q1 = NPN-Transistor [mpn=NPN package="TO92 [THT]"]
  D1 = V-REFERENCE [part_number=6V2 package=sot23-3]
  C2 = Ceramic Capacitor [capacitance=100nF voltage=35V package="200 mil [THT, multilayer]"]
  D2 = Schottky Diode [part_number=Schottky package="300 mil [THT]"]
  C1 = Electrolytic Capacitor [capacitance=220µF voltage=35V package="0405 [SMD, electrolytic]"]
  D1_2 = V-REFERENCE [part_number=6V8 package=sot23-3]
  C1_2 = Electrolytic Capacitor [capacitance=220µF voltage=35V package="0405 [SMD, electrolytic]"]
  D2_2 = Schottky Diode [part_number=Schottky package="300 mil [THT]"]

nets:
  Charger-/GND/PV-: Q1.E, C1.-, D1_2.A, C1_2.-
  N1: Q1.B, D1.A, C2.0
  PV+: Q1.C, D1.C, C2.1, D2.anode, D1_2.C, D2_2.anode
  Charger+: D2.cathode, C1.+, C1_2.+, D2_2.cathode

notes:
  1. Make sure Q1's power is enough to shunt the current
  2. Q1's beta should be small, otherwise the current through D1 is too weak
  3. C2 avoids oscillation, place it as close as possible to Q1
  Zener + BJT clamp for 6V solar panel
  Zener clamp for 6V solar panel
  1. Make sure D1 power is enough (it acts also as reverse polarity shunt)
  2. C1 levels the output
  3. D2 limits reverse current flow back from C1 through D1 or the solar panel
  Charger with max input of 6.5V
